# Fritzing sketch Perfboard (saved by Fritzing 0.9.3b)
perfboards: 2

parts:
  R1 = PHOTOCELL [package=photocell]
  Part1 = Arduino Nano (Rev3.0) (ICSP)
  LED1 = LED - 3mm [color="White (6500K)" package="3 mm [THT]"]
  R2 = Resistor [tolerance=±5% resistance=15k package=THT]
  R3 = Resistor [tolerance=±5% resistance=1 package=THT]

nets:
  N1: R1.P$1, Part1.A0, R2.Pin_0
  N2: R1.P$2, Part1.3V3, LED1.anode
  N3: Part1.GND, R2.Pin_1, R3.Pin_1
  N4: LED1.cathode, R3.Pin_0
